// Logisim project CPU(CS46).circ as structural Verilog: 4 circuits, main circuit CPU
module ALU (
  input  [31:0] A,
  input  [31:0] B,
  input  in_3,
  input  in_4,
  input  [2:0] OPN,
  output ADD,
  output out_7,
  output [31:0] OUT
);

  wire [31:0] adder_1_out, and_1_out, or_1_out, subtractor_1_out, xor_1_out;

  Adder #(.width(32)) adder_1 (.a(A), .b(B), .out(adder_1_out), .cin(in_3), .cout(ADD));
  Subtractor #(.width(32)) subtractor_1 (.a(A), .b(B), .out(subtractor_1_out), .bin(in_4), .bout(out_7));
  assign or_1_out = A | B;  // OR_Gate or_1, 32 bits wide
  assign and_1_out = A & B;  // AND_Gate and_1, 32 bits wide
  assign xor_1_out = A ^ B;  // XOR_Gate xor_1, 32 bits wide
  Multiplexer #(.select(3), .width(32)) multiplexer_1 (
    .in0(adder_1_out), .in1(subtractor_1_out), .in2(or_1_out), .in3(and_1_out), .in4(xor_1_out), .in5(A),
    .out(OUT), .sel(OPN));  // open: in6, in7, en

  // Notes on the sheet:
  //   OR
  //   AND
  //   SUB
  //   XOR
  //   MOVE
endmodule

module CPU (
  input  in_1
);

  wire C, clock_1_out, MOP, P, shift_register_1_out;
  wire [2:0] AR;
  wire [4:0] A, B, C_t;
  wire [11:0] shift_register_1_q31;
  wire [23:0] bit_extender_1_out;
  wire [31:0] alu_1_out, Ins, IV, multiplexer_1_out, multiplexer_2_out, multiplexer_3_out, RA_q, RB_q,
       rf_1_ra, rf_1_rb, RM_q, RY_q, RZ_q;

  RF rf_1 (.A(A), .B(B), .RC(RY_q), .Clo(C), .RA(rf_1_ra), .RB(rf_1_rb), .C(C_t));
  Register #(.width(32)) RA (.D(rf_1_ra), .Q(RA_q), .clk(C));  // open: en, clr
  Register #(.width(32)) RB (.D(rf_1_rb), .Q(RB_q), .clk(C));  // open: en, clr
  ALU alu_1 (.OPN(AR), .A(RA_q), .B(multiplexer_2_out), .OUT(alu_1_out));  // open: in_3, ADD, in_4, out_7
  Register #(.width(32)) RZ (.D(alu_1_out), .Q(RZ_q), .clk(C));  // open: en, clr
  Multiplexer #(.width(32)) multiplexer_1 (
    .in0(RZ_q), .in1(multiplexer_3_out), .out(multiplexer_1_out), .sel(MOP));  // open: en
  Multiplexer #(.width(32)) multiplexer_2 (.in0(RB_q), .in1(IV), .out(multiplexer_2_out), .sel(P));  // open: en
  Register #(.width(32)) RY (.D(multiplexer_1_out), .Q(RY_q), .clk(C));  // open: en, clr
  Register #(.width(32)) RM (.D(RB_q), .Q(RM_q), .clk(C));  // open: en, clr
  Bit_Extender #(.in_width(32), .out_width(24)) bit_extender_1 (.in(RZ_q), .out(bit_extender_1_out));
  Shift_Register #(.length(32)) shift_register_1 (
    .shift(in_1), .in(shift_register_1_out), .clk(C), .out(shift_register_1_out), .load(1'b1), .d0(Ins[31]),
    .q0(MOP), .d1(Ins[30]), .q1(AR[2]), .d2(Ins[29]), .q2(AR[1]), .d3(Ins[28]), .q3(AR[0]), .d4(Ins[27]),
    .q4(C_t[4]), .d5(Ins[26]), .q5(C_t[3]), .d6(Ins[25]), .q6(C_t[2]), .d7(Ins[24]), .q7(C_t[1]),
    .d8(Ins[23]), .q8(C_t[0]), .d9(Ins[22]), .q9(A[4]), .d10(Ins[21]), .q10(A[3]), .d11(Ins[20]), .q11(A[2]),
    .d12(Ins[19]), .q12(A[1]), .d13(Ins[18]), .q13(A[0]), .d14(Ins[17]), .q14(B[4]), .d15(Ins[16]),
    .q15(B[3]), .d16(Ins[15]), .q16(B[2]), .d17(Ins[14]), .q17(B[1]), .d18(Ins[13]), .q18(B[0]),
    .d19(Ins[12]), .q19(P), .d20(Ins[11]), .q20(shift_register_1_q31[11]), .d21(Ins[10]),
    .q21(shift_register_1_q31[10]), .d22(Ins[9]), .q22(shift_register_1_q31[9]), .d23(Ins[8]),
    .q23(shift_register_1_q31[8]), .d24(Ins[7]), .q24(shift_register_1_q31[7]), .d25(Ins[6]),
    .q25(shift_register_1_q31[6]), .d26(Ins[5]), .q26(shift_register_1_q31[5]), .d27(Ins[4]),
    .q27(shift_register_1_q31[4]), .d28(Ins[3]), .q28(shift_register_1_q31[3]), .d29(Ins[2]),
    .q29(shift_register_1_q31[2]), .d30(Ins[1]), .q30(shift_register_1_q31[1]), .d31(Ins[0]),
    .q31(shift_register_1_q31[0]));  // open: clr
  Multiplexer #(.width(32)) multiplexer_3 (.in0(RM_q), .out(multiplexer_3_out), .sel(AR[2]));  // open: in1, en
  RAM #(.addrWidth(24), .dataWidth(32)) ram_1 (
    .addr(bit_extender_1_out), .data(multiplexer_3_out), .sel(MOP), .clk(C), .ld(AR[2]));  // open: clr
  Clock #(.highDuration(8), .lowDuration(8)) clock_1 (.out(clock_1_out));
  Clock clock_2 (.out(C));
  assign IV = {{20{1'b0}}, shift_register_1_q31};  // Bit_Extender bit_extender_2
  PC pc_1 (.out_1(Ins));

  // Other names for the same wires on the sheet: LOAD = AR[2]

  // Notes on the sheet:
  //   (5)
  //   (4)
  //   Opcode
  //   R des
  //   (5)
  //   R src2
  //   (1)
  //   (5)
  //   flag
  //   (12)
  //   Imm Value
endmodule

module RF (
  input  [4:0] A,
  input  [4:0] C,
  input  [4:0] B,
  input  [31:0] RC,
  input  Clo,
  output [31:0] RB,
  output [31:0] RA
);

  wire decoder_1_out0, decoder_1_out1, decoder_1_out2, decoder_1_out3, decoder_1_out4, decoder_1_out5,
       decoder_1_out6, decoder_1_out7, decoder_1_out8, decoder_1_out9, decoder_1_out10, decoder_1_out11,
       decoder_1_out12, decoder_1_out13, decoder_1_out14, decoder_1_out15, decoder_1_out16, decoder_1_out17,
       decoder_1_out18, decoder_1_out19, decoder_1_out20, decoder_1_out21, decoder_1_out22, decoder_1_out23,
       decoder_1_out24, decoder_1_out25, decoder_1_out26, decoder_1_out27, decoder_1_out28, decoder_1_out29,
       decoder_1_out30, decoder_1_out31;
  wire [31:0] demultiplexer_1_out0, demultiplexer_1_out1, demultiplexer_1_out2, demultiplexer_1_out3,
       demultiplexer_1_out4, demultiplexer_1_out5, demultiplexer_1_out6, demultiplexer_1_out7,
       demultiplexer_1_out8, demultiplexer_1_out9, demultiplexer_1_out10, demultiplexer_1_out11,
       demultiplexer_1_out12, demultiplexer_1_out13, demultiplexer_1_out14, demultiplexer_1_out15,
       demultiplexer_1_out16, demultiplexer_1_out17, demultiplexer_1_out18, demultiplexer_1_out19,
       demultiplexer_1_out20, demultiplexer_1_out21, demultiplexer_1_out22, demultiplexer_1_out23,
       demultiplexer_1_out24, demultiplexer_1_out25, demultiplexer_1_out26, demultiplexer_1_out27,
       demultiplexer_1_out28, demultiplexer_1_out29, demultiplexer_1_out30, demultiplexer_1_out31, R1_q,
       R2_q, R3_q, R4_q, R5_q, R6_q, R7_q, R8_q, R9_q, R10_q, R11_q, R12_q, R13_q, R14_q, R15_q, R16_q,
       R17_q, R18_q, R19_q, R20_q, R21_q, R22_q, R23_q, R24_q, R25_q, R26_q, R27_q, R28_q, R29_q, R30_q,
       R31_q, R32_q;

  Multiplexer #(.select(5), .width(32), .disabled(0)) multiplexer_1 (
    .in0(R1_q), .in1(R2_q), .in2(R3_q), .in3(R4_q), .in4(R5_q), .in5(R6_q), .in6(R7_q), .in7(R8_q),
    .in8(R9_q), .in9(R10_q), .in10(R11_q), .in11(R12_q), .in12(R13_q), .in13(R14_q), .in14(R15_q),
    .in15(R16_q), .in16(R17_q), .in17(R18_q), .in18(R19_q), .in19(R20_q), .in20(R21_q), .in21(R22_q),
    .in22(R23_q), .in23(R24_q), .in24(R25_q), .in25(R26_q), .in26(R27_q), .in27(R28_q), .in28(R29_q),
    .in29(R30_q), .in30(R31_q), .in31(R32_q), .out(RA), .sel(A));  // open: en
  Multiplexer #(.select(5), .width(32), .disabled(0)) multiplexer_2 (
    .in0(R1_q), .in1(R2_q), .in2(R3_q), .in3(R4_q), .in4(R5_q), .in5(R6_q), .in6(R7_q), .in7(R8_q),
    .in8(R9_q), .in9(R10_q), .in10(R11_q), .in11(R12_q), .in12(R13_q), .in13(R14_q), .in14(R15_q),
    .in15(R16_q), .in16(R17_q), .in17(R18_q), .in18(R19_q), .in19(R20_q), .in20(R21_q), .in21(R22_q),
    .in22(R23_q), .in23(R24_q), .in24(R25_q), .in25(R26_q), .in26(R27_q), .in27(R28_q), .in28(R29_q),
    .in29(R30_q), .in30(R31_q), .in31(R32_q), .out(RB), .sel(B));  // open: en
  Demultiplexer #(.select(5), .width(32), .disabled(0)) demultiplexer_1 (
    .out0(demultiplexer_1_out0), .out1(demultiplexer_1_out1), .out2(demultiplexer_1_out2),
    .out3(demultiplexer_1_out3), .out4(demultiplexer_1_out4), .out5(demultiplexer_1_out5),
    .out6(demultiplexer_1_out6), .out7(demultiplexer_1_out7), .out8(demultiplexer_1_out8),
    .out9(demultiplexer_1_out9), .out10(demultiplexer_1_out10), .out11(demultiplexer_1_out11),
    .out12(demultiplexer_1_out12), .out13(demultiplexer_1_out13), .out14(demultiplexer_1_out14),
    .out15(demultiplexer_1_out15), .out16(demultiplexer_1_out16), .out17(demultiplexer_1_out17),
    .out18(demultiplexer_1_out18), .out19(demultiplexer_1_out19), .out20(demultiplexer_1_out20),
    .out21(demultiplexer_1_out21), .out22(demultiplexer_1_out22), .out23(demultiplexer_1_out23),
    .out24(demultiplexer_1_out24), .out25(demultiplexer_1_out25), .out26(demultiplexer_1_out26),
    .out27(demultiplexer_1_out27), .out28(demultiplexer_1_out28), .out29(demultiplexer_1_out29),
    .out30(demultiplexer_1_out30), .out31(demultiplexer_1_out31), .in(RC), .sel(C));  // open: en
  Register #(.width(32)) R1 (.D(demultiplexer_1_out0), .en(decoder_1_out0), .Q(R1_q), .clk(Clo));  // open: clr
  Register #(.width(32)) R5 (.D(demultiplexer_1_out4), .en(decoder_1_out4), .Q(R5_q), .clk(Clo));  // open: clr
  Register #(.width(32)) R9 (.D(demultiplexer_1_out8), .en(decoder_1_out8), .Q(R9_q), .clk(Clo));  // open: clr
  Register #(.width(32)) R13 (.D(demultiplexer_1_out12), .en(decoder_1_out12), .Q(R13_q), .clk(Clo));  // open: clr
  Register #(.width(32)) R17 (.D(demultiplexer_1_out16), .en(decoder_1_out16), .Q(R17_q), .clk(Clo));  // open: clr
  Register #(.width(32)) R21 (.D(demultiplexer_1_out20), .en(decoder_1_out20), .Q(R21_q), .clk(Clo));  // open: clr
  Register #(.width(32)) R25 (.D(demultiplexer_1_out24), .en(decoder_1_out24), .Q(R25_q), .clk(Clo));  // open: clr
  Register #(.width(32)) R29 (.D(demultiplexer_1_out28), .en(decoder_1_out28), .Q(R29_q), .clk(Clo));  // open: clr
  Register #(.width(32)) R2 (.D(demultiplexer_1_out1), .en(decoder_1_out1), .Q(R2_q), .clk(Clo));  // open: clr
  Register #(.width(32)) R6 (.D(demultiplexer_1_out5), .en(decoder_1_out5), .Q(R6_q), .clk(Clo));  // open: clr
  Register #(.width(32)) R10 (.D(demultiplexer_1_out9), .en(decoder_1_out9), .Q(R10_q), .clk(Clo));  // open: clr
  Register #(.width(32)) R14 (.D(demultiplexer_1_out13), .en(decoder_1_out13), .Q(R14_q), .clk(Clo));  // open: clr
  Register #(.width(32)) R18 (.D(demultiplexer_1_out17), .en(decoder_1_out17), .Q(R18_q), .clk(Clo));  // open: clr
  Register #(.width(32)) R22 (.D(demultiplexer_1_out21), .en(decoder_1_out21), .Q(R22_q), .clk(Clo));  // open: clr
  Register #(.width(32)) R26 (.D(demultiplexer_1_out25), .en(decoder_1_out25), .Q(R26_q), .clk(Clo));  // open: clr
  Register #(.width(32)) R30 (.D(demultiplexer_1_out29), .en(decoder_1_out29), .Q(R30_q), .clk(Clo));  // open: clr
  Register #(.width(32)) R3 (.D(demultiplexer_1_out2), .en(decoder_1_out2), .Q(R3_q), .clk(Clo));  // open: clr
  Register #(.width(32)) R7 (.D(demultiplexer_1_out6), .en(decoder_1_out6), .Q(R7_q), .clk(Clo));  // open: clr
  Register #(.width(32)) R11 (.D(demultiplexer_1_out10), .en(decoder_1_out10), .Q(R11_q), .clk(Clo));  // open: clr
  Register #(.width(32)) R15 (.D(demultiplexer_1_out14), .en(decoder_1_out14), .Q(R15_q), .clk(Clo));  // open: clr
  Register #(.width(32)) R19 (.D(demultiplexer_1_out18), .en(decoder_1_out18), .Q(R19_q), .clk(Clo));  // open: clr
  Register #(.width(32)) R23 (.D(demultiplexer_1_out22), .en(decoder_1_out22), .Q(R23_q), .clk(Clo));  // open: clr
  Register #(.width(32)) R27 (.D(demultiplexer_1_out26), .en(decoder_1_out26), .Q(R27_q), .clk(Clo));  // open: clr
  Register #(.width(32)) R31 (.D(demultiplexer_1_out30), .en(decoder_1_out30), .Q(R31_q), .clk(Clo));  // open: clr
  Register #(.width(32)) R4 (.D(demultiplexer_1_out3), .en(decoder_1_out3), .Q(R4_q), .clk(Clo));  // open: clr
  Register #(.width(32)) R8 (.D(demultiplexer_1_out7), .en(decoder_1_out7), .Q(R8_q), .clk(Clo));  // open: clr
  Register #(.width(32)) R12 (.D(demultiplexer_1_out11), .en(decoder_1_out11), .Q(R12_q), .clk(Clo));  // open: clr
  Register #(.width(32)) R16 (.D(demultiplexer_1_out15), .en(decoder_1_out15), .Q(R16_q), .clk(Clo));  // open: clr
  Register #(.width(32)) R20 (.D(demultiplexer_1_out19), .en(decoder_1_out19), .Q(R20_q), .clk(Clo));  // open: clr
  Register #(.width(32)) R24 (.D(demultiplexer_1_out23), .en(decoder_1_out23), .Q(R24_q), .clk(Clo));  // open: clr
  Register #(.width(32)) R28 (.D(demultiplexer_1_out27), .en(decoder_1_out27), .Q(R28_q), .clk(Clo));  // open: clr
  Register #(.width(32)) R32 (.D(demultiplexer_1_out31), .en(decoder_1_out31), .Q(R32_q), .clk(Clo));  // open: clr
  Decoder #(.select(5)) decoder_1 (
    .out0(decoder_1_out0), .out1(decoder_1_out1), .out2(decoder_1_out2), .out3(decoder_1_out3),
    .out4(decoder_1_out4), .out5(decoder_1_out5), .out6(decoder_1_out6), .out7(decoder_1_out7),
    .out8(decoder_1_out8), .out9(decoder_1_out9), .out10(decoder_1_out10), .out11(decoder_1_out11),
    .out12(decoder_1_out12), .out13(decoder_1_out13), .out14(decoder_1_out14), .out15(decoder_1_out15),
    .out16(decoder_1_out16), .out17(decoder_1_out17), .out18(decoder_1_out18), .out19(decoder_1_out19),
    .out20(decoder_1_out20), .out21(decoder_1_out21), .out22(decoder_1_out22), .out23(decoder_1_out23),
    .out24(decoder_1_out24), .out25(decoder_1_out25), .out26(decoder_1_out26), .out27(decoder_1_out27),
    .out28(decoder_1_out28), .out29(decoder_1_out29), .out30(decoder_1_out30), .out31(decoder_1_out31),
    .sel(C));  // open: en
endmodule

module PC (
  output [31:0] out_1
);

  wire clock_1_out;
  wire [23:0] bit_extender_1_out;
  wire [31:0] adder_1_out, PC_q;

  Clock #(.highDuration(8), .lowDuration(8)) clock_1 (.out(clock_1_out));
  Register #(.width(32)) PC (.D(adder_1_out), .en(1'b1), .Q(PC_q), .clk(clock_1_out));  // open: clr
  Adder #(.width(32)) adder_1 (.a(PC_q), .b(32'h1), .out(adder_1_out), .cin(1'b0));  // open: cout
  Bit_Extender #(.in_width(32), .out_width(24)) bit_extender_1 (.in(PC_q), .out(bit_extender_1_out));
  ROM #(.addrWidth(24), .dataWidth(32)) rom_1 (.addr(bit_extender_1_out), .data(out_1));  // open: sel
endmodule
